// Logisim project lab-1-multiple.circ as structural Verilog: 1 circuit, main circuit main
module main (
  input  S1,
  input  S2,
  input  S3,
  input  S4,
  input  S1_2,
  input  S2_2,
  input  S3_2,
  input  S4_2,
  input  S1_3,
  input  S2_3,
  input  S3_3,
  input  S4_3,
  input  S1_4,
  input  S2_4,
  input  S3_4,
  input  S4_4,
  output Door_1,
  output Door_1_2,
  output Door_2,
  output Door_2_2,
  output Door_1_3,
  output Door_1_4,
  output Door_2_3,
  output Door_2_4
);

  wire and_1_out, and_2_out, and_3_out, and_4_out, nor_1_out, nor_2_out, nor_3_out, nor_4_out, nor_5_out,
       nor_6_out, nor_7_out, nor_8_out, nor_9_out, nor_12_out, nor_13_out, nor_14_out, nor_15_out,
       nor_16_out, nor_17_out, nor_18_out, nor_19_out, not_1_out, not_2_out, not_3_out, not_4_out, not_5_out,
       not_6_out, not_7_out, not_8_out, not_11_out, not_12_out, not_13_out, not_14_out, not_15_out,
       not_16_out, not_17_out, not_18_out, not_19_out, not_20_out, not_21_out, not_22_out, not_23_out,
       not_24_out, not_25_out, not_26_out, not_27_out, not_28_out, not_29_out, not_30_out, not_31_out,
       not_32_out, not_33_out;

  not not_1 (not_1_out, S1);
  not not_2 (not_2_out, S1_4);
  not not_3 (not_3_out, S2);
  not not_4 (not_4_out, S3);
  not not_5 (not_5_out, S2_4);
  not not_6 (not_6_out, S3_4);
  not not_7 (not_7_out, S4);
  not not_8 (not_8_out, S4_4);
  nor nor_1 (nor_1_out, S1, S4);
  nor nor_2 (nor_2_out, S1, not_4_out);
  nor nor_3 (nor_3_out, not_1_out, not_7_out);
  nor nor_4 (nor_4_out, S3, not_7_out);
  nor nor_5 (nor_5_out, not_4_out, S4);
  nor nor_6 (nor_6_out, not_2_out, S2_4, S4_4);
  nor nor_7 (nor_7_out, S1_4, S2_4, S3_4, not_8_out);
  nor nor_8 (nor_8_out, not_2_out, S2_4, S3_4, S4_4);
  nor nor_9 (nor_9_out, not_2_out, S2_4, not_6_out, not_8_out);
  nor nor_10 (Door_1, S2, nor_1_out, nor_2_out, nor_3_out);
  nor nor_11 (Door_2_2, not_1_out, S2, nor_4_out, nor_5_out);
  nor nor_12 (nor_12_out, nor_6_out, nor_7_out);
  not not_9 (Door_1_4, nor_12_out);
  not not_10 (Door_2_4, nor_13_out);
  nor nor_13 (nor_13_out, nor_8_out, nor_9_out);
  not not_11 (not_11_out, S1_2);
  not not_12 (not_12_out, S2_2);
  not not_13 (not_13_out, S2_3);
  not not_14 (not_14_out, S1_3);
  not not_15 (not_15_out, S4_2);
  not not_16 (not_16_out, S3_2);
  not not_17 (not_17_out, S3_3);
  not not_18 (not_18_out, S4_3);
  not not_19 (not_19_out, S1_3);
  not not_20 (not_20_out, not_13_out);
  not not_21 (not_21_out, not_18_out);
  not not_22 (not_22_out, not_14_out);
  not not_23 (not_23_out, not_13_out);
  not not_24 (not_24_out, not_17_out);
  not not_25 (not_25_out, S4_3);
  not not_26 (not_26_out, S1_3);
  not not_27 (not_27_out, not_13_out);
  not not_28 (not_28_out, not_17_out);
  not not_29 (not_29_out, not_18_out);
  not not_30 (not_30_out, S1_3);
  not not_31 (not_31_out, not_13_out);
  not not_32 (not_32_out, S3_3);
  not not_33 (not_33_out, S4_3);
  and and_1 (and_1_out, S1_2, not_12_out, not_15_out);
  and and_2 (and_2_out, not_11_out, not_12_out, not_16_out, S4_2);
  and and_3 (and_3_out, S1_2, not_12_out, not_16_out, not_15_out);
  and and_4 (and_4_out, S1_2, not_12_out, S3_2, S4_2);
  nor nor_14 (nor_14_out, not_19_out, not_20_out, not_21_out);
  nor nor_15 (nor_15_out, not_22_out, not_23_out, not_24_out, not_25_out);
  nor nor_16 (nor_16_out, not_26_out, not_27_out, not_28_out, not_29_out);
  nor nor_17 (nor_17_out, not_30_out, not_31_out, not_32_out, not_33_out);
  or or_1 (Door_1_2, and_1_out, and_2_out);
  or or_2 (Door_2, and_3_out, and_4_out);
  not not_34 (Door_1_3, nor_18_out);
  nor nor_18 (nor_18_out, nor_14_out, nor_15_out);
  nor nor_19 (nor_19_out, nor_16_out, nor_17_out);
  not not_35 (Door_2_3, nor_19_out);
endmodule
