// Logisim project lab-1.circ as structural Verilog: 1 circuit, main circuit main
module main (
  input  S1,
  input  S2,
  input  S3,
  input  S4,
  output Door_1,
  output Door_2
);

  wire nor_1_out, nor_2_out, nor_3_out, nor_4_out, nor_5_out, not_1_out, not_2_out, not_3_out, not_4_out;

  not not_1 (not_1_out, S1);
  not not_2 (not_2_out, S2);
  not not_3 (not_3_out, S3);
  not not_4 (not_4_out, S4);
  nor nor_1 (nor_1_out, S1, S4);
  nor nor_2 (nor_2_out, S1, not_3_out);
  nor nor_3 (nor_3_out, not_1_out, not_4_out);
  nor nor_4 (nor_4_out, S3, not_4_out);
  nor nor_5 (nor_5_out, not_3_out, S4);
  nor nor_6 (Door_1, S2, nor_1_out, nor_2_out, nor_3_out);
  nor nor_7 (Door_2, not_1_out, S2, nor_4_out, nor_5_out);

  // Notes on the sheet:
  //   Door Circuit
endmodule
