// Logisim project Multiplexer.circ as structural Verilog: 1 circuit, main circuit main
module main (
  input  L1,
  input  S1,
  input  S0
);

  wire and_1_out, and_2_out, and_3_out, and_4_out, and_5_out, and_6_out, and_7_out, and_8_out, not_1_out,
       not_2_out, not_3_out, not_4_out;

  not not_1 (not_1_out, S0);
  not not_2 (not_2_out, S1);
  not not_3 (not_3_out, not_2_out);
  not not_4 (not_4_out, not_1_out);
  and and_1 (and_1_out, not_1_out, not_2_out);
  and and_2 (and_2_out, not_4_out, not_2_out);
  and and_3 (and_3_out, not_1_out, not_3_out);
  and and_4 (and_4_out, not_4_out, not_3_out);
  and and_5 (and_5_out, not_1_out, not_2_out);
  and and_6 (and_6_out, not_4_out, not_2_out);
  and and_7 (and_7_out, not_1_out, not_3_out);
  and and_8 (and_8_out, not_4_out, not_3_out);
  // OR_Gate or_1 has open pins: in0=and_1_out, in1=and_2_out, in2=and_3_out, in3=and_4_out, out=open
  // OR_Gate or_2 has open pins: in0=and_5_out, in1=and_6_out, in2=and_7_out, in3=and_8_out, out=open
endmodule
