// Logisim project lab-2-ground.circ as structural Verilog: 1 circuit, main circuit main
module main (
  input  S1,
  input  S2,
  input  S3,
  input  S4,
  input  S1_2,
  input  S0,
  output Door_1,
  output Door_2
);

  wire and_1_out, and_2_out, and_3_out, and_4_out, and_5_out, and_6_out, and_7_out, and_8_out, nor_1_out,
       nor_2_out, nor_3_out, nor_4_out, nor_5_out, nor_6_out, nor_7_out, not_1_out, not_2_out, not_3_out,
       not_4_out, not_5_out, not_6_out, not_7_out, not_8_out, or_1_out, or_2_out;

  not not_1 (not_1_out, S1);
  not not_2 (not_2_out, S0);
  not not_3 (not_3_out, S1_2);
  not not_4 (not_4_out, not_2_out);
  not not_5 (not_5_out, not_3_out);
  not not_6 (not_6_out, S2);
  not not_7 (not_7_out, S3);
  not not_8 (not_8_out, S4);
  and and_1 (and_1_out, not_2_out, not_3_out);
  and and_2 (and_2_out, not_4_out, not_3_out);
  and and_3 (and_3_out, not_2_out, 1'b0, not_5_out);
  and and_4 (and_4_out, not_4_out, 1'b0, not_5_out);
  and and_5 (and_5_out, not_2_out, not_3_out);
  and and_6 (and_6_out, not_4_out, 1'b0, not_3_out);
  and and_7 (and_7_out, not_2_out, not_5_out);
  and and_8 (and_8_out, not_4_out, 1'b0, not_5_out);
  nor nor_1 (nor_1_out, S1, S4);
  nor nor_2 (nor_2_out, S1, not_7_out);
  nor nor_3 (nor_3_out, not_1_out, not_8_out);
  nor nor_4 (nor_4_out, S3, not_8_out);
  nor nor_5 (nor_5_out, not_7_out, S4);
  nor nor_6 (nor_6_out, S2, nor_1_out, nor_2_out, nor_3_out);
  nor nor_7 (nor_7_out, not_1_out, S2, nor_4_out, nor_5_out);
  or or_1 (or_1_out, and_1_out, and_2_out, and_3_out, and_4_out);
  or or_2 (or_2_out, and_5_out, and_6_out, and_7_out, and_8_out);
  and and_9 (Door_1, nor_6_out, or_1_out);
  and and_10 (Door_2, nor_7_out, or_2_out);

  // Notes on the sheet:
  //   L1
  //   Door Circuit
  //   Multiplexer Security Override
  //   1y
  //   2y
endmodule
