// Logisim project Lab-3-wDebug.circ as structural Verilog: 1 circuit, main circuit main
module main (
  input  SDI,
  input  Rst_10101,
  input  Rst_11000,
  input  Rst_0,
  input  Rst_1,
  output out_6
);

  wire clock_1_out, d_ff_1_q, d_ff_2_q, d_ff_3_q, d_ff_4_q, d_ff_5_q, nor_1_out, nor_2_out, nor_3_out,
       not_1_out, not_2_out, not_3_out, not_4_out, not_5_out, or_1_out, or_2_out, or_3_out, or_4_out,
       or_5_out, or_6_out, or_7_out, or_8_out;

  or or_1 (or_1_out, Rst_10101, Rst_11000, Rst_1);
  not not_1 (not_1_out, d_ff_1_q);
  Clock clock_1 (.out(clock_1_out));
  not not_2 (not_2_out, d_ff_2_q);
  not not_3 (not_3_out, d_ff_4_q);
  not not_4 (not_4_out, d_ff_3_q);
  D_Flip_Flop d_ff_1 (.clk(clock_1_out), .D(SDI), .Q(d_ff_1_q), .preset(or_1_out), .reset(Rst_0));  // open: Qn, en
  or or_2 (or_2_out, Rst_11000, Rst_1);
  not not_5 (not_5_out, d_ff_5_q);
  D_Flip_Flop d_ff_2 (
    .clk(clock_1_out), .D(d_ff_1_q), .Q(d_ff_2_q), .preset(or_2_out), .reset(or_4_out));  // open: Qn, en
  or or_3 (or_3_out, Rst_10101, Rst_1);
  or or_4 (or_4_out, Rst_10101, Rst_0);
  nor nor_1 (nor_1_out, not_2_out, not_4_out);
  nor nor_2 (nor_2_out, d_ff_3_q, not_5_out);
  nor nor_3 (nor_3_out, d_ff_2_q, d_ff_5_q);
  D_Flip_Flop d_ff_3 (
    .clk(clock_1_out), .D(d_ff_2_q), .Q(d_ff_3_q), .preset(or_3_out), .reset(or_5_out));  // open: Qn, en
  or or_5 (or_5_out, Rst_11000, Rst_0);
  D_Flip_Flop d_ff_4 (.clk(clock_1_out), .D(d_ff_3_q), .Q(d_ff_4_q), .preset(Rst_1), .reset(or_6_out));  // open: Qn, en
  nor nor_4 (out_6, not_1_out, d_ff_4_q, nor_1_out, nor_2_out, nor_3_out);
  D_Flip_Flop d_ff_5 (
    .clk(clock_1_out), .D(d_ff_4_q), .Q(d_ff_5_q), .preset(or_8_out), .reset(or_7_out));  // open: Qn, en
  or or_6 (or_6_out, Rst_10101, Rst_11000, Rst_0);
  or or_7 (or_7_out, Rst_11000, Rst_0);
  or or_8 (or_8_out, Rst_10101, Rst_1);

  // Notes on the sheet:
  //   Clk
  //   S0
  //   S3
  //   S2
  //   S1
  //   S4
endmodule
