// Logisim project Lab-3.circ as structural Verilog: 1 circuit, main circuit main
module main (
  input  Clk,
  input  SDI,
  input  Rst_0,
  input  Rst_1,
  output out_5
);

  wire d_ff_1_q, d_ff_2_q, d_ff_3_q, d_ff_4_q, d_ff_5_q, nor_1_out, nor_2_out, nor_3_out, not_1_out,
       not_2_out, not_3_out, not_4_out, not_5_out;

  not not_1 (not_1_out, d_ff_1_q);
  not not_2 (not_2_out, d_ff_3_q);
  not not_3 (not_3_out, d_ff_2_q);
  D_Flip_Flop d_ff_1 (.clk(Clk), .D(SDI), .Q(d_ff_1_q), .preset(Rst_1), .reset(Rst_0));  // open: Qn, en
  not not_4 (not_4_out, d_ff_5_q);
  not not_5 (not_5_out, d_ff_4_q);
  D_Flip_Flop d_ff_2 (.clk(Clk), .D(d_ff_1_q), .Q(d_ff_2_q), .preset(Rst_1), .reset(Rst_0));  // open: Qn, en
  nor nor_1 (nor_1_out, not_3_out, not_2_out);
  nor nor_2 (nor_2_out, d_ff_3_q, not_4_out);
  nor nor_3 (nor_3_out, d_ff_2_q, d_ff_5_q);
  D_Flip_Flop d_ff_3 (.clk(Clk), .D(d_ff_2_q), .Q(d_ff_3_q), .preset(Rst_1), .reset(Rst_0));  // open: Qn, en
  D_Flip_Flop d_ff_4 (.clk(Clk), .D(d_ff_3_q), .Q(d_ff_4_q), .preset(Rst_1), .reset(Rst_0));  // open: Qn, en
  nor nor_4 (out_5, not_1_out, d_ff_4_q, nor_1_out, nor_2_out, nor_3_out);
  D_Flip_Flop d_ff_5 (.clk(Clk), .D(d_ff_4_q), .Q(d_ff_5_q), .preset(Rst_1), .reset(Rst_0));  // open: Qn, en

  // Notes on the sheet:
  //   S0
  //   S2
  //   S1
  //   S3
  //   S4
endmodule
